// Logisim project hw4.circ as structural Verilog: 1 circuit, main circuit main
module main (
);

  D_Flip_Flop d_ff_1 ();  // open: clk, D, Q, Qn, preset, reset
  ROM Instruction_Memory ();  // open: addr, data
  RAM Data_Memory ();  // open: addr, data, sel, clk, ld, clr
endmodule
